# Fritzing sketch arm (saved by Fritzing 0.8.7b)
breadboards: 1

parts:
  VCC1 = 4 x AAA Battery Mount
  R1 = Rotary Potentiometer (Small) [maximum_resistance=100kΩ package=THT]
  J1 = Basic Servo
  J2 = Basic Servo
  J3 = Basic Servo
  J4 = Basic Servo
  R2 = Rotary Potentiometer (Small) [maximum_resistance=100kΩ package=THT]
  R3 = Rotary Potentiometer (Small) [maximum_resistance=100kΩ package=THT]
  R4 = Rotary Potentiometer (Small) [maximum_resistance=100kΩ package=THT]
  Part1 = Arduino Uno (Rev3)

nets:
  GND: VCC1.-, J1.gnd, J2.gnd, J3.gnd, J4.gnd
  N1: VCC1.+, R1.leg1, R2.leg1, R3.leg1, R4.leg1
  N2: R1.wiper, Part1.A0
  N3: R1.leg2, J1.vcc
  N4: J1.pulse, Part1.D10_PWM/SS
  N5: J2.vcc, R2.leg2
  N6: J2.pulse, Part1.D9_PWM
  N7: J3.vcc, R3.leg2
  N8: J3.pulse, Part1.D12/MISO
  N9: J4.vcc, R4.leg2
  N10: J4.pulse, Part1.D11_PWM/MOSI
  N11: R2.wiper, Part1.A1
  N12: R3.wiper, Part1.A2
  N13: R4.wiper, Part1.A3
